# Fritzing sketch Wemos D1 Mini + ILI9341 (saved by Fritzing 0.9.4)

parts:
  WeMos_D1_Mini1 = WeMos D1 Mini
  LCD2 = 2.8" SPI TFT Module [part_number=MSP2807]

nets:
  N1: WeMos_D1_Mini1.3V3, LCD2.pin1
  N2: WeMos_D1_Mini1.D0, LCD2.pin4
  N3: WeMos_D1_Mini1.D1, LCD2.pin5
  N4: WeMos_D1_Mini1.D2, LCD2.pin3
  N5: WeMos_D1_Mini1.D5, LCD2.pin7
  N6: WeMos_D1_Mini1.D7, LCD2.pin6
  N7: WeMos_D1_Mini1.G, LCD2.pin2

notes:
  VCC
  GND
  SCK
  SDI
  RES
  DC
  CS
  LED
  GND = GND
  VCC = 3V3
  SCK = D5
  SDI = D7
  RES = D0
  DC = D1
  CS = D2
  LED = 3V3

custom parts:
  2.8" SPI TFT Module: A generic 2.8 inch LCD TFT 320x240 display with touchscreen and SD card slot. Uses the ILI9341 controller, like the Adafruit displays of this size uses.
