# Fritzing sketch Schaltplan 5110 (saved by Fritzing 0.9.4)

parts:
  WeMos_D1_Mini1 = WeMos D1 Mini
  Nokia_5110_LCD_Module1 = Nokia 5110 LCD

nets:
  N1: WeMos_D1_Mini1.3V3, Nokia_5110_LCD_Module1.DN(MOSI), Nokia_5110_LCD_Module1.DN(MODI)_(out)
  N2: WeMos_D1_Mini1.D0, Nokia_5110_LCD_Module1.VCC, Nokia_5110_LCD_Module1.VCC_(out)
  N3: WeMos_D1_Mini1.D1, Nokia_5110_LCD_Module1.SCE, Nokia_5110_LCD_Module1.SCE_(out)
  N4: WeMos_D1_Mini1.D2, Nokia_5110_LCD_Module1.GND, Nokia_5110_LCD_Module1.GND_(out)
  N5: WeMos_D1_Mini1.D5, Nokia_5110_LCD_Module1.D/C, Nokia_5110_LCD_Module1.D/C_(out)
  N6: WeMos_D1_Mini1.D7, Nokia_5110_LCD_Module1.RST, Nokia_5110_LCD_Module1.RST_(out)
  N7: WeMos_D1_Mini1.G, Nokia_5110_LCD_Module1.LED, Nokia_5110_LCD_Module1.LED_(out)

notes:
  VCC
  GND
  CLK
  DIN
  RES
  DC
  CE
  LIGHT
  GND = GND
  VCC = 3V3
  CLK = D5
  DIN = D7
  RES = D0
  DC = D1
  CE = D2
  LIGHT = 3V3

custom parts:
  Nokia 5110 LCD: Nokia 5110 Graphic 84*48 LCD module such as the Sparkfun LCD-10168 or the clones from Ebay. There is example code for the Arduino available from the Sparkfun site in https://learn.sparkfun.com/tutorials/graphic-lcd-hookup-guide This is a 3.3V device, if you are running it from a 5V micro you need a 5V tolorant level translator such as the 74ahc367 to protect the signal imputs. Rafa G. did a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
